// Logisim project logisim.circ as structural Verilog: 28 circuits, main circuit main
module main (
  input  opcode,
  input  in_2,
  input  reg1,
  input  in_4,
  input  reg2,
  input  in_6,
  input  reg3,
  input  in_8,
  input  in_9,
  input  in_10,
  input  in_11,
  input  in_12,
  input  in_13,
  input  in_14,
  input  Reset,
  input  in_16
);

  wire addr16reg8b_1_out_15, addr16reg8b_1_out_16, addr16reg8b_1_out_17, addr16reg8b_1_out_18,
       addr16reg8b_1_out_19, addr16reg8b_1_out_20, addr16reg8b_1_out_21, addr16reg8b_1_out_22, and_1_out,
       and_2_out, and_3_out, clock_1_out, clock_2_out, nor_1_out, not_1_out, onehotencoder2b_1_out_3,
       or_1_out, programcounter4b_1_out_8, programcounter4b_1_out_9, programcounter4b_1_out_10,
       programcounter4b_1_out_11, programcounter4b_1_out_12, registermanager4b_1_out_16,
       registermanager4b_1_out_17, registermanager4b_1_out_18, registermanager4b_1_out_19,
       registermanager4b_1_out_20, selector4b_1_out_10, selector4b_1_out_11, selector4b_1_out_12,
       selector4b_1_out_13, selector4b_2_out_10, selector4b_2_out_11, selector4b_2_out_12,
       selector4b_2_out_13;

  Clock #(.highDuration(5), .lowDuration(30)) clock_1 (.out(clock_1_out));
  selector4b selector4b_1 (
    .in_1(addr16reg8b_1_out_19), .in_2(addr16reg8b_1_out_20), .in_3(addr16reg8b_1_out_21),
    .in_4(addr16reg8b_1_out_22), .in_5(1'b0), .in_6(1'b0), .in_7(1'b0), .in_8(1'b0), .in_9(in_16),
    .out_10(selector4b_1_out_10), .out_11(selector4b_1_out_11), .out_12(selector4b_1_out_12),
    .out_13(selector4b_1_out_13));
  and and_1 (and_1_out, in_10, clock_1_out);
  programCounter4b programcounter4b_1 (
    .out_8(programcounter4b_1_out_8), .out_9(programcounter4b_1_out_9), .out_10(programcounter4b_1_out_10),
    .out_11(programcounter4b_1_out_11), .out_12(programcounter4b_1_out_12), .Clock(and_1_out),
    .in_2(selector4b_1_out_10), .in_3(selector4b_1_out_11), .Next_value(selector4b_1_out_12),
    .in_5(selector4b_1_out_13), .in_6(or_1_out), .Reset(Reset));
  or or_1 (or_1_out, in_16, and_3_out);
  and and_2 (and_2_out, in_9, not_1_out);
  not not_1 (not_1_out, in_10);
  selector4b selector4b_2 (
    .in_1(in_11), .in_2(in_12), .in_3(in_13), .in_4(in_14), .in_5(programcounter4b_1_out_8),
    .in_6(programcounter4b_1_out_9), .in_7(programcounter4b_1_out_10), .in_8(programcounter4b_1_out_11),
    .in_9(in_10), .out_10(selector4b_2_out_10), .out_11(selector4b_2_out_11), .out_12(selector4b_2_out_12),
    .out_13(selector4b_2_out_13));
  addr16reg8b addr16reg8b_1 (
    .in_1(opcode), .in_2(in_2), .in_3(reg1), .in_4(in_4), .Value_to_write(reg2), .in_6(in_6), .in_7(reg3),
    .in_8(in_8), .Read___Write(and_2_out), .in_10(selector4b_2_out_10), .in_11(selector4b_2_out_11),
    .in_12(selector4b_2_out_12), .out_15(addr16reg8b_1_out_15), .out_16(addr16reg8b_1_out_16),
    .out_17(addr16reg8b_1_out_17), .out_18(addr16reg8b_1_out_18), .out_19(addr16reg8b_1_out_19),
    .out_20(addr16reg8b_1_out_20), .out_21(addr16reg8b_1_out_21), .out_22(addr16reg8b_1_out_22),
    .in_13(selector4b_2_out_13), .in_14(Reset));
  oneHotEncoder2b onehotencoder2b_1 (
    .in_1(addr16reg8b_1_out_15), .in_2(addr16reg8b_1_out_16), .out_3(onehotencoder2b_1_out_3));  // open: out_4, out_5, out_6
  and and_3 (and_3_out, onehotencoder2b_1_out_3, registermanager4b_1_out_20, nor_1_out);
  Clock clock_2 (.out(clock_2_out));
  registerManager4b registermanager4b_1 (
    .opcode(addr16reg8b_1_out_15), .in_2(addr16reg8b_1_out_16), .addr1(addr16reg8b_1_out_17),
    .in_4(addr16reg8b_1_out_18), .addr2(addr16reg8b_1_out_19), .in_6(addr16reg8b_1_out_20),
    .addr3(addr16reg8b_1_out_21), .in_8(addr16reg8b_1_out_22), .in_9(addr16reg8b_1_out_19),
    .value(addr16reg8b_1_out_20), .in_11(addr16reg8b_1_out_21), .in_12(addr16reg8b_1_out_22),
    .init(clock_1_out), .reset(Reset), .out_16(registermanager4b_1_out_16),
    .out_17(registermanager4b_1_out_17), .out_18(registermanager4b_1_out_18),
    .out_19(registermanager4b_1_out_19), .out_20(registermanager4b_1_out_20), .clock(clock_2_out));
  nor nor_1 (nor_1_out, registermanager4b_1_out_16, registermanager4b_1_out_17, registermanager4b_1_out_18, registermanager4b_1_out_19);

  // Notes on the sheet:
  //   Initialise pointer to zero
  //   To write instruction
  //   Instruction adress to write
  //   /
  //   value
  //   Launch program
  //   Write instruction
endmodule

module addElem (
  input  in_1,
  input  in_2,
  output out_3,
  output out_4
);

  xor xor_1 (out_3, in_1, in_2);
  and and_1 (out_4, in_1, in_2);
endmodule

module addRetenue (
  input  in_1,
  input  in_2,
  input  in_3,
  output out_4,
  output out_5
);

  wire addelem_1_out_3, addelem_1_out_4, addelem_2_out_4;

  addElem addelem_1 (.in_1(in_2), .in_2(in_3), .out_3(addelem_1_out_3), .out_4(addelem_1_out_4));
  addElem addelem_2 (.in_1(in_1), .in_2(addelem_1_out_3), .out_3(out_4), .out_4(addelem_2_out_4));
  or or_1 (out_5, addelem_2_out_4, addelem_1_out_4);
endmodule

module add4b (
  input  in_1,
  input  in_2,
  input  in_3,
  input  in_4,
  input  in_5,
  input  in_6,
  input  in_7,
  input  in_8,
  output out_9,
  output out_10,
  output out_11,
  output out_12,
  output out_13
);

  wire addretenue_1_out_5, addretenue_2_out_5, addretenue_3_out_5;

  addRetenue addretenue_1 (.in_1(1'b0), .in_2(in_1), .in_3(in_5), .out_4(out_9), .out_5(addretenue_1_out_5));
  addRetenue addretenue_2 (
    .in_1(addretenue_1_out_5), .in_2(in_2), .in_3(in_6), .out_4(out_10), .out_5(addretenue_2_out_5));
  addRetenue addretenue_3 (
    .in_1(addretenue_2_out_5), .in_2(in_3), .in_3(in_7), .out_4(out_11), .out_5(addretenue_3_out_5));
  addRetenue addretenue_4 (.in_1(addretenue_3_out_5), .in_2(in_4), .in_3(in_8), .out_4(out_12), .out_5(out_13));
endmodule

module mult4b (
  input  in_1,
  input  in_2,
  input  in_3,
  input  in_4,
  input  in_5,
  input  in_6,
  input  in_7,
  input  in_8,
  output out_9,
  output out_10,
  output out_11,
  output out_12
);

  wire add4b_1_out_9, add4b_1_out_10, add4b_1_out_11, add4b_1_out_12, add4b_2_out_9, add4b_2_out_10,
       add4b_2_out_11, add4b_2_out_12, selector4b_1_out_10, selector4b_1_out_11, selector4b_1_out_12,
       selector4b_1_out_13, selector4b_2_out_10, selector4b_2_out_11, selector4b_2_out_12,
       selector4b_2_out_13, selector4b_3_out_10, selector4b_3_out_11, selector4b_3_out_12,
       selector4b_3_out_13, selector4b_4_out_10, selector4b_4_out_11, selector4b_4_out_12,
       selector4b_4_out_13;

  selector4b selector4b_1 (
    .in_1(1'b0), .in_2(1'b0), .in_3(1'b0), .in_4(1'b0), .in_5(in_1), .in_6(in_2), .in_7(in_3), .in_8(in_4),
    .in_9(in_5), .out_10(selector4b_1_out_10), .out_11(selector4b_1_out_11), .out_12(selector4b_1_out_12),
    .out_13(selector4b_1_out_13));
  selector4b selector4b_2 (
    .in_1(1'b0), .in_2(1'b0), .in_3(1'b0), .in_4(1'b0), .in_5(1'b0), .in_6(in_1), .in_7(in_2), .in_8(in_3),
    .in_9(in_6), .out_10(selector4b_2_out_10), .out_11(selector4b_2_out_11), .out_12(selector4b_2_out_12),
    .out_13(selector4b_2_out_13));
  add4b add4b_1 (
    .in_1(selector4b_1_out_10), .in_2(selector4b_1_out_11), .in_3(selector4b_1_out_12),
    .in_4(selector4b_1_out_13), .in_5(selector4b_2_out_10), .in_6(selector4b_2_out_11),
    .in_7(selector4b_2_out_12), .in_8(selector4b_2_out_13), .out_9(add4b_1_out_9), .out_10(add4b_1_out_10),
    .out_11(add4b_1_out_11), .out_12(add4b_1_out_12));  // open: out_13
  selector4b selector4b_3 (
    .in_1(1'b0), .in_2(1'b0), .in_3(1'b0), .in_4(1'b0), .in_5(1'b0), .in_6(1'b0), .in_7(in_1), .in_8(in_2),
    .in_9(in_7), .out_10(selector4b_3_out_10), .out_11(selector4b_3_out_11), .out_12(selector4b_3_out_12),
    .out_13(selector4b_3_out_13));
  selector4b selector4b_4 (
    .in_1(1'b0), .in_2(1'b0), .in_3(1'b0), .in_4(1'b0), .in_5(1'b0), .in_6(1'b0), .in_7(1'b0), .in_8(in_1),
    .in_9(in_8), .out_10(selector4b_4_out_10), .out_11(selector4b_4_out_11), .out_12(selector4b_4_out_12),
    .out_13(selector4b_4_out_13));
  add4b add4b_2 (
    .in_1(add4b_1_out_9), .in_2(add4b_1_out_10), .in_3(add4b_1_out_11), .in_4(add4b_1_out_12),
    .in_5(selector4b_3_out_10), .in_6(selector4b_3_out_11), .in_7(selector4b_3_out_12),
    .in_8(selector4b_3_out_13), .out_9(add4b_2_out_9), .out_10(add4b_2_out_10), .out_11(add4b_2_out_11),
    .out_12(add4b_2_out_12));  // open: out_13
  add4b add4b_3 (
    .in_1(add4b_2_out_9), .in_2(add4b_2_out_10), .in_3(add4b_2_out_11), .in_4(add4b_2_out_12),
    .in_5(selector4b_4_out_10), .in_6(selector4b_4_out_11), .in_7(selector4b_4_out_12),
    .in_8(selector4b_4_out_13), .out_9(out_9), .out_10(out_10), .out_11(out_11), .out_12(out_12));  // open: out_13
endmodule

module selector4b (
  input  in_1,
  input  in_2,
  input  in_3,
  input  in_4,
  input  in_5,
  input  in_6,
  input  in_7,
  input  in_8,
  input  in_9,
  output out_10,
  output out_11,
  output out_12,
  output out_13
);

  selector_1b selector_1b_1 (.in_1(in_1), .in_2(in_5), .in_3(in_9), .out_4(out_10));
  selector_1b selector_1b_2 (.in_1(in_2), .in_2(in_6), .in_3(in_9), .out_4(out_11));
  selector_1b selector_1b_3 (.in_1(in_3), .in_2(in_7), .in_3(in_9), .out_4(out_12));
  selector_1b selector_1b_4 (.in_1(in_4), .in_2(in_8), .in_3(in_9), .out_4(out_13));
endmodule

module selector_1b (
  input  in_1,
  input  in_2,
  input  in_3,
  output out_4
);

  wire and_1_out, and_2_out, not_1_out;

  not not_1 (not_1_out, in_3);
  and and_1 (and_1_out, in_1, not_1_out);
  and and_2 (and_2_out, in_2, in_3);
  or or_1 (out_4, and_1_out, and_2_out);
endmodule

module sous4b (
  input  in_1,
  input  in_2,
  input  in_3,
  input  in_4,
  input  in_5,
  input  in_6,
  input  in_7,
  input  in_8,
  output out_9,
  output out_10,
  output out_11,
  output out_12,
  output out_13
);

  wire neg4b_1_out_5, neg4b_1_out_6, neg4b_1_out_7, neg4b_1_out_8;

  neg4b neg4b_1 (
    .in_1(in_5), .in_2(in_6), .in_3(in_7), .in_4(in_8), .out_5(neg4b_1_out_5), .out_6(neg4b_1_out_6),
    .out_7(neg4b_1_out_7), .out_8(neg4b_1_out_8));
  add4b add4b_1 (
    .in_1(in_1), .in_2(in_2), .in_3(in_3), .in_4(in_4), .in_5(neg4b_1_out_5), .in_6(neg4b_1_out_6),
    .in_7(neg4b_1_out_7), .in_8(neg4b_1_out_8), .out_9(out_9), .out_10(out_10), .out_11(out_11),
    .out_12(out_12), .out_13(out_13));
endmodule

module neg4b (
  input  in_1,
  input  in_2,
  input  in_3,
  input  in_4,
  output out_5,
  output out_6,
  output out_7,
  output out_8
);

  wire not_1_out, not_2_out, not_3_out, not_4_out;

  not not_1 (not_1_out, in_1);
  not not_2 (not_2_out, in_2);
  not not_3 (not_3_out, in_3);
  not not_4 (not_4_out, in_4);
  add4b add4b_1 (
    .in_1(not_1_out), .in_2(not_2_out), .in_3(not_3_out), .in_4(not_4_out), .in_5(1'b1), .in_6(1'b0),
    .in_7(1'b0), .in_8(1'b0), .out_9(out_5), .out_10(out_6), .out_11(out_7), .out_12(out_8));  // open: out_13
endmodule

module ALU4b (
  input  in_1,
  input  in_2,
  input  in_3,
  input  in_4,
  input  in_5,
  input  in_6,
  input  in_7,
  input  in_8,
  input  in_9,
  input  in_10,
  output out_11,
  output out_12,
  output out_13,
  output out_14
);

  wire add4b_1_out_9, add4b_1_out_10, add4b_1_out_11, add4b_1_out_12, mult4b_1_out_9, mult4b_1_out_10,
       mult4b_1_out_11, mult4b_1_out_12, onehotencoder2b_1_out_4, onehotencoder2b_1_out_5,
       selector4b_1_out_10, selector4b_1_out_11, selector4b_1_out_12, selector4b_1_out_13, sous4b_1_out_9,
       sous4b_1_out_10, sous4b_1_out_11, sous4b_1_out_12;

  oneHotEncoder2b onehotencoder2b_1 (
    .in_1(in_9), .in_2(in_10), .out_4(onehotencoder2b_1_out_4), .out_5(onehotencoder2b_1_out_5));  // open: out_3, out_6
  add4b add4b_1 (
    .in_1(in_1), .in_2(in_2), .in_3(in_3), .in_4(in_4), .in_5(in_5), .in_6(in_6), .in_7(in_7), .in_8(in_8),
    .out_9(add4b_1_out_9), .out_10(add4b_1_out_10), .out_11(add4b_1_out_11), .out_12(add4b_1_out_12));  // open: out_13
  sous4b sous4b_1 (
    .in_1(in_1), .in_2(in_2), .in_3(in_3), .in_4(in_4), .in_5(in_5), .in_6(in_6), .in_7(in_7), .in_8(in_8),
    .out_9(sous4b_1_out_9), .out_10(sous4b_1_out_10), .out_11(sous4b_1_out_11), .out_12(sous4b_1_out_12));  // open: out_13
  mult4b mult4b_1 (
    .in_1(in_1), .in_2(in_2), .in_3(in_3), .in_4(in_4), .in_5(in_5), .in_6(in_6), .in_7(in_7), .in_8(in_8),
    .out_9(mult4b_1_out_9), .out_10(mult4b_1_out_10), .out_11(mult4b_1_out_11), .out_12(mult4b_1_out_12));
  selector4b selector4b_1 (
    .in_1(add4b_1_out_9), .in_2(add4b_1_out_10), .in_3(add4b_1_out_11), .in_4(add4b_1_out_12),
    .in_5(sous4b_1_out_9), .in_6(sous4b_1_out_10), .in_7(sous4b_1_out_11), .in_8(sous4b_1_out_12),
    .in_9(onehotencoder2b_1_out_4), .out_10(selector4b_1_out_10), .out_11(selector4b_1_out_11),
    .out_12(selector4b_1_out_12), .out_13(selector4b_1_out_13));
  selector4b selector4b_2 (
    .in_1(selector4b_1_out_10), .in_2(selector4b_1_out_11), .in_3(selector4b_1_out_12),
    .in_4(selector4b_1_out_13), .in_5(mult4b_1_out_9), .in_6(mult4b_1_out_10), .in_7(mult4b_1_out_11),
    .in_8(mult4b_1_out_12), .in_9(onehotencoder2b_1_out_5), .out_10(out_11), .out_11(out_12),
    .out_12(out_13), .out_13(out_14));
endmodule

module oneHotEncoder2b (
  input  in_1,
  input  in_2,
  output out_3,
  output out_4,
  output out_5,
  output out_6
);

  wire not_1_out, not_2_out, not_3_out, not_4_out;

  not not_1 (not_1_out, in_1);
  and and_1 (out_3, not_1_out, not_2_out);
  not not_2 (not_2_out, in_2);
  and and_2 (out_4, in_1, not_3_out);
  not not_3 (not_3_out, in_2);
  not not_4 (not_4_out, in_1);
  and and_3 (out_5, not_4_out, in_2);
  and and_4 (out_6, in_1, in_2);
endmodule

module ALU4b2op (
  input  in_1,
  input  in_2,
  input  Number_1,
  input  in_4,
  input  in_5,
  input  in_6,
  input  Number_2,
  input  in_8,
  input  Add___Substract,
  output out_10,
  output out_11,
  output out_12,
  output out_13
);

  wire add4b_1_out_9, add4b_1_out_10, add4b_1_out_11, add4b_1_out_12, sous4b_1_out_9, sous4b_1_out_10,
       sous4b_1_out_11, sous4b_1_out_12;

  add4b add4b_1 (
    .in_1(in_1), .in_2(in_2), .in_3(Number_1), .in_4(in_4), .in_5(in_5), .in_6(in_6), .in_7(Number_2),
    .in_8(in_8), .out_9(add4b_1_out_9), .out_10(add4b_1_out_10), .out_11(add4b_1_out_11),
    .out_12(add4b_1_out_12));  // open: out_13
  sous4b sous4b_1 (
    .in_1(in_1), .in_2(in_2), .in_3(Number_1), .in_4(in_4), .in_5(in_5), .in_6(in_6), .in_7(Number_2),
    .in_8(in_8), .out_9(sous4b_1_out_9), .out_10(sous4b_1_out_10), .out_11(sous4b_1_out_11),
    .out_12(sous4b_1_out_12));  // open: out_13
  selector4b selector4b_1 (
    .in_1(add4b_1_out_9), .in_2(add4b_1_out_10), .in_3(add4b_1_out_11), .in_4(add4b_1_out_12),
    .in_5(sous4b_1_out_9), .in_6(sous4b_1_out_10), .in_7(sous4b_1_out_11), .in_8(sous4b_1_out_12),
    .in_9(Add___Substract), .out_10(out_10), .out_11(out_11), .out_12(out_12), .out_13(out_13));
endmodule

module mem1b (
  input  Value_to_write,
  input  Read___Write,
  input  Reset,
  output out_4
);

  wire and_1_out, and_2_out, not_1_out, or_1_out;

  and and_1 (and_1_out, Value_to_write, Read___Write);
  D_Flip_Flop d_ff_1 (.Q(out_4), .preset(and_1_out), .reset(or_1_out));  // open: clk, D, Qn, en
  or or_1 (or_1_out, and_2_out, Reset);
  and and_2 (and_2_out, Read___Write, not_1_out);
  not not_1 (not_1_out, Value_to_write);
endmodule

module mem2b (
  input  in_1,
  input  Value_to_write,
  input  Read___Write,
  input  Reset,
  output out_5,
  output out_6
);

  mem1b mem1b_1 (.Value_to_write(in_1), .Read___Write(Read___Write), .Reset(Reset), .out_4(out_5));
  mem1b mem1b_2 (.Value_to_write(Value_to_write), .Read___Write(Read___Write), .Reset(Reset), .out_4(out_6));
endmodule

module mem4b (
  input  in_1,
  input  in_2,
  input  in_3,
  input  in_4,
  input  Reset,
  input  Read___Write,
  output out_7,
  output out_8,
  output out_9,
  output out_10
);

  mem2b mem2b_1 (
    .in_1(in_1), .Value_to_write(in_2), .Read___Write(Read___Write), .out_5(out_7), .out_6(out_8),
    .Reset(Reset));
  mem2b mem2b_2 (
    .in_1(in_3), .Value_to_write(in_4), .Read___Write(Read___Write), .out_5(out_9), .out_6(out_10),
    .Reset(Reset));

  // Notes on the sheet:
  //   Value to write
endmodule

module mem8b (
  input  in_1,
  input  in_2,
  input  in_3,
  input  in_4,
  input  in_5,
  input  in_6,
  input  in_7,
  input  in_8,
  input  in_9,
  input  Read___Write,
  output out_11,
  output out_12,
  output out_13,
  output out_14,
  output out_15,
  output out_16,
  output out_17,
  output out_18
);

  mem4b mem4b_1 (
    .in_1(in_1), .in_2(in_2), .in_3(in_3), .in_4(in_5), .Read___Write(Read___Write), .out_7(out_11),
    .out_8(out_12), .out_9(out_13), .out_10(out_14), .Reset(in_4));
  mem4b mem4b_2 (
    .in_1(in_6), .in_2(in_7), .in_3(in_8), .in_4(in_9), .Read___Write(Read___Write), .out_7(out_15),
    .out_8(out_16), .out_9(out_17), .out_10(out_18), .Reset(in_4));

  // Notes on the sheet:
  //   Value to write
endmodule

module adrr4reg4b (
  input  in_1,
  input  in_2,
  input  Value_to_write,
  input  in_4,
  input  Read___Write,
  input  in_6,
  input  Register_adress,
  input  Reset,
  output out_9,
  output out_10,
  output out_11,
  output out_12
);

  wire and_1_out, and_2_out, and_3_out, and_4_out, mem4b_1_out_7, mem4b_1_out_8, mem4b_1_out_9,
       mem4b_1_out_10, mem4b_2_out_7, mem4b_2_out_8, mem4b_2_out_9, mem4b_2_out_10, mem4b_3_out_7,
       mem4b_3_out_8, mem4b_3_out_9, mem4b_3_out_10, mem4b_4_out_7, mem4b_4_out_8, mem4b_4_out_9,
       mem4b_4_out_10, onehotencoder2b_1_out_3, onehotencoder2b_1_out_4, onehotencoder2b_1_out_5,
       onehotencoder2b_1_out_6, selector4b_1_out_10, selector4b_1_out_11, selector4b_1_out_12,
       selector4b_1_out_13, selector4b_2_out_10, selector4b_2_out_11, selector4b_2_out_12,
       selector4b_2_out_13;

  oneHotEncoder2b onehotencoder2b_1 (
    .in_1(in_6), .in_2(Register_adress), .out_3(onehotencoder2b_1_out_3), .out_4(onehotencoder2b_1_out_4),
    .out_5(onehotencoder2b_1_out_5), .out_6(onehotencoder2b_1_out_6));
  and and_1 (and_1_out, Read___Write, onehotencoder2b_1_out_3);
  and and_2 (and_2_out, Read___Write, onehotencoder2b_1_out_4);
  and and_3 (and_3_out, Read___Write, onehotencoder2b_1_out_5);
  and and_4 (and_4_out, Read___Write, onehotencoder2b_1_out_6);
  mem4b mem4b_1 (
    .in_1(in_1), .in_2(in_2), .in_3(Value_to_write), .in_4(in_4), .Read___Write(and_1_out),
    .out_7(mem4b_1_out_7), .out_8(mem4b_1_out_8), .out_9(mem4b_1_out_9), .out_10(mem4b_1_out_10),
    .Reset(Reset));
  mem4b mem4b_2 (
    .in_1(in_1), .in_2(in_2), .in_3(Value_to_write), .in_4(in_4), .Read___Write(and_2_out),
    .out_7(mem4b_2_out_7), .out_8(mem4b_2_out_8), .out_9(mem4b_2_out_9), .out_10(mem4b_2_out_10),
    .Reset(Reset));
  mem4b mem4b_3 (
    .in_1(in_1), .in_2(in_2), .in_3(Value_to_write), .in_4(in_4), .Read___Write(and_3_out),
    .out_7(mem4b_3_out_7), .out_8(mem4b_3_out_8), .out_9(mem4b_3_out_9), .out_10(mem4b_3_out_10),
    .Reset(Reset));
  mem4b mem4b_4 (
    .in_1(in_1), .in_2(in_2), .in_3(Value_to_write), .in_4(in_4), .Read___Write(and_4_out),
    .out_7(mem4b_4_out_7), .out_8(mem4b_4_out_8), .out_9(mem4b_4_out_9), .out_10(mem4b_4_out_10),
    .Reset(Reset));
  selector4b selector4b_1 (
    .in_1(mem4b_1_out_7), .in_2(mem4b_1_out_8), .in_3(mem4b_1_out_9), .in_4(mem4b_1_out_10),
    .in_5(mem4b_2_out_7), .in_6(mem4b_2_out_8), .in_7(mem4b_2_out_9), .in_8(mem4b_2_out_10), .in_9(in_6),
    .out_10(selector4b_1_out_10), .out_11(selector4b_1_out_11), .out_12(selector4b_1_out_12),
    .out_13(selector4b_1_out_13));
  selector4b selector4b_2 (
    .in_1(mem4b_3_out_7), .in_2(mem4b_3_out_8), .in_3(mem4b_3_out_9), .in_4(mem4b_3_out_10),
    .in_5(mem4b_4_out_7), .in_6(mem4b_4_out_8), .in_7(mem4b_4_out_9), .in_8(mem4b_4_out_10), .in_9(in_6),
    .out_10(selector4b_2_out_10), .out_11(selector4b_2_out_11), .out_12(selector4b_2_out_12),
    .out_13(selector4b_2_out_13));
  selector4b selector4b_3 (
    .in_1(selector4b_1_out_10), .in_2(selector4b_1_out_11), .in_3(selector4b_1_out_12),
    .in_4(selector4b_1_out_13), .in_5(selector4b_2_out_10), .in_6(selector4b_2_out_11),
    .in_7(selector4b_2_out_12), .in_8(selector4b_2_out_13), .in_9(Register_adress), .out_10(out_9),
    .out_11(out_10), .out_12(out_11), .out_13(out_12));
endmodule

module addr4reg8b (
  input  in_1,
  input  in_2,
  input  in_3,
  input  in_4,
  input  in_5,
  input  in_6,
  input  in_7,
  input  in_8,
  input  Read___Write,
  input  in_10,
  input  Register_adress,
  input  Reset,
  output out_13,
  output out_14,
  output out_15,
  output out_16,
  output out_17,
  output out_18,
  output out_19,
  output out_20
);

  adrr4reg4b adrr4reg4b_1 (
    .in_1(in_1), .in_2(in_2), .Value_to_write(in_3), .in_4(in_4), .Read___Write(Read___Write), .in_6(in_10),
    .Register_adress(Register_adress), .out_9(out_13), .out_10(out_14), .out_11(out_15), .out_12(out_16),
    .Reset(Reset));
  adrr4reg4b adrr4reg4b_2 (
    .in_1(in_5), .in_2(in_6), .Value_to_write(in_7), .in_4(in_8), .Read___Write(Read___Write), .in_6(in_10),
    .Register_adress(Register_adress), .out_9(out_17), .out_10(out_18), .out_11(out_19), .out_12(out_20),
    .Reset(Reset));

  // Notes on the sheet:
  //   Value to write
endmodule

module addr16reg8b (
  input  in_1,
  input  in_2,
  input  in_3,
  input  in_4,
  input  Value_to_write,
  input  in_6,
  input  in_7,
  input  in_8,
  input  Read___Write,
  input  in_10,
  input  in_11,
  input  in_12,
  input  in_13,
  input  in_14,
  output out_15,
  output out_16,
  output out_17,
  output out_18,
  output out_19,
  output out_20,
  output out_21,
  output out_22
);

  wire addr8reg8b_1_out_14, addr8reg8b_1_out_15, addr8reg8b_1_out_16, addr8reg8b_1_out_17,
       addr8reg8b_1_out_18, addr8reg8b_1_out_19, addr8reg8b_1_out_20, addr8reg8b_1_out_21,
       addr8reg8b_2_out_14, addr8reg8b_2_out_15, addr8reg8b_2_out_16, addr8reg8b_2_out_17,
       addr8reg8b_2_out_18, addr8reg8b_2_out_19, addr8reg8b_2_out_20, addr8reg8b_2_out_21, and_1_out,
       and_2_out, not_1_out;

  not not_1 (not_1_out, in_13);
  and and_1 (and_1_out, Read___Write, not_1_out);
  and and_2 (and_2_out, Read___Write, in_13);
  addr8reg8b addr8reg8b_1 (
    .in_1(in_1), .in_2(in_2), .in_3(in_3), .in_4(in_4), .Value_to_write(Value_to_write), .in_6(in_6),
    .in_7(in_7), .in_8(in_8), .Read___Write(and_1_out), .in_10(in_10), .in_11(in_11), .in_12(in_12),
    .out_14(addr8reg8b_1_out_14), .out_15(addr8reg8b_1_out_15), .out_16(addr8reg8b_1_out_16),
    .out_17(addr8reg8b_1_out_17), .out_18(addr8reg8b_1_out_18), .out_19(addr8reg8b_1_out_19),
    .out_20(addr8reg8b_1_out_20), .out_21(addr8reg8b_1_out_21), .Reset(in_14));
  addr8reg8b addr8reg8b_2 (
    .in_1(in_1), .in_2(in_2), .in_3(in_3), .in_4(in_4), .Value_to_write(Value_to_write), .in_6(in_6),
    .in_7(in_7), .in_8(in_8), .Read___Write(and_2_out), .in_10(in_10), .in_11(in_11), .in_12(in_12),
    .out_14(addr8reg8b_2_out_14), .out_15(addr8reg8b_2_out_15), .out_16(addr8reg8b_2_out_16),
    .out_17(addr8reg8b_2_out_17), .out_18(addr8reg8b_2_out_18), .out_19(addr8reg8b_2_out_19),
    .out_20(addr8reg8b_2_out_20), .out_21(addr8reg8b_2_out_21), .Reset(in_14));
  selector8b selector8b_1 (
    .in_1(addr8reg8b_1_out_14), .in_2(addr8reg8b_1_out_15), .in_3(addr8reg8b_1_out_16),
    .in_4(addr8reg8b_1_out_17), .in_5(addr8reg8b_1_out_18), .in_6(addr8reg8b_1_out_19),
    .in_7(addr8reg8b_1_out_20), .in_8(addr8reg8b_1_out_21), .in_9(addr8reg8b_2_out_14),
    .in_10(addr8reg8b_2_out_15), .in_11(addr8reg8b_2_out_16), .in_12(addr8reg8b_2_out_17),
    .in_13(addr8reg8b_2_out_18), .in_14(addr8reg8b_2_out_19), .in_15(addr8reg8b_2_out_20),
    .in_16(addr8reg8b_2_out_21), .in_17(in_13), .out_18(out_15), .out_19(out_16), .out_20(out_17),
    .out_21(out_18), .out_22(out_19), .out_23(out_20), .out_24(out_21), .out_25(out_22));

  // Notes on the sheet:
  //   Register adress
endmodule

module addr8reg8b (
  input  in_1,
  input  in_2,
  input  in_3,
  input  in_4,
  input  Value_to_write,
  input  in_6,
  input  in_7,
  input  in_8,
  input  Read___Write,
  input  in_10,
  input  in_11,
  input  in_12,
  input  Reset,
  output out_14,
  output out_15,
  output out_16,
  output out_17,
  output out_18,
  output out_19,
  output out_20,
  output out_21
);

  wire addr4reg8b_1_out_13, addr4reg8b_1_out_14, addr4reg8b_1_out_15, addr4reg8b_1_out_16,
       addr4reg8b_1_out_17, addr4reg8b_1_out_18, addr4reg8b_1_out_19, addr4reg8b_1_out_20,
       addr4reg8b_2_out_13, addr4reg8b_2_out_14, addr4reg8b_2_out_15, addr4reg8b_2_out_16,
       addr4reg8b_2_out_17, addr4reg8b_2_out_18, addr4reg8b_2_out_19, addr4reg8b_2_out_20, and_1_out,
       and_2_out, not_1_out;

  and and_1 (and_1_out, Read___Write, not_1_out);
  not not_1 (not_1_out, in_12);
  and and_2 (and_2_out, Read___Write, in_12);
  addr4reg8b addr4reg8b_1 (
    .in_1(in_1), .in_2(in_2), .in_3(in_3), .in_4(in_4), .in_5(Value_to_write), .in_6(in_6), .in_7(in_7),
    .in_8(in_8), .Read___Write(and_1_out), .in_10(in_10), .Register_adress(in_11),
    .out_13(addr4reg8b_1_out_13), .out_14(addr4reg8b_1_out_14), .out_15(addr4reg8b_1_out_15),
    .out_16(addr4reg8b_1_out_16), .out_17(addr4reg8b_1_out_17), .out_18(addr4reg8b_1_out_18),
    .out_19(addr4reg8b_1_out_19), .out_20(addr4reg8b_1_out_20), .Reset(Reset));
  addr4reg8b addr4reg8b_2 (
    .in_1(in_1), .in_2(in_2), .in_3(in_3), .in_4(in_4), .in_5(Value_to_write), .in_6(in_6), .in_7(in_7),
    .in_8(in_8), .Read___Write(and_2_out), .in_10(in_10), .Register_adress(in_11),
    .out_13(addr4reg8b_2_out_13), .out_14(addr4reg8b_2_out_14), .out_15(addr4reg8b_2_out_15),
    .out_16(addr4reg8b_2_out_16), .out_17(addr4reg8b_2_out_17), .out_18(addr4reg8b_2_out_18),
    .out_19(addr4reg8b_2_out_19), .out_20(addr4reg8b_2_out_20), .Reset(Reset));
  selector8b selector8b_1 (
    .in_1(addr4reg8b_1_out_13), .in_2(addr4reg8b_1_out_14), .in_3(addr4reg8b_1_out_15),
    .in_4(addr4reg8b_1_out_16), .in_5(addr4reg8b_1_out_17), .in_6(addr4reg8b_1_out_18),
    .in_7(addr4reg8b_1_out_19), .in_8(addr4reg8b_1_out_20), .in_9(addr4reg8b_2_out_13),
    .in_10(addr4reg8b_2_out_14), .in_11(addr4reg8b_2_out_15), .in_12(addr4reg8b_2_out_16),
    .in_13(addr4reg8b_2_out_17), .in_14(addr4reg8b_2_out_18), .in_15(addr4reg8b_2_out_19),
    .in_16(addr4reg8b_2_out_20), .in_17(in_12), .out_18(out_14), .out_19(out_15), .out_20(out_16),
    .out_21(out_17), .out_22(out_18), .out_23(out_19), .out_24(out_20), .out_25(out_21));

  // Notes on the sheet:
  //   Register adress
endmodule

module selector8b (
  input  in_1,
  input  in_2,
  input  in_3,
  input  in_4,
  input  in_5,
  input  in_6,
  input  in_7,
  input  in_8,
  input  in_9,
  input  in_10,
  input  in_11,
  input  in_12,
  input  in_13,
  input  in_14,
  input  in_15,
  input  in_16,
  input  in_17,
  output out_18,
  output out_19,
  output out_20,
  output out_21,
  output out_22,
  output out_23,
  output out_24,
  output out_25
);

  selector4b selector4b_1 (
    .in_1(in_1), .in_2(in_2), .in_3(in_3), .in_4(in_4), .in_5(in_9), .in_6(in_10), .in_7(in_11),
    .in_8(in_12), .in_9(in_17), .out_10(out_18), .out_11(out_19), .out_12(out_20), .out_13(out_21));
  selector4b selector4b_2 (
    .in_1(in_5), .in_2(in_6), .in_3(in_7), .in_4(in_8), .in_5(in_13), .in_6(in_14), .in_7(in_15),
    .in_8(in_16), .in_9(in_17), .out_10(out_22), .out_11(out_23), .out_12(out_24), .out_13(out_25));
endmodule

module programCounter4b (
  input  Clock,
  input  in_2,
  input  in_3,
  input  Next_value,
  input  in_5,
  input  in_6,
  input  Reset,
  output out_8,
  output out_9,
  output out_10,
  output out_11,
  output out_12
);

  wire add4b_1_out_9, add4b_1_out_10, add4b_1_out_11, add4b_1_out_12, mem4b_2_out_7, mem4b_2_out_8,
       mem4b_2_out_9, mem4b_2_out_10, not_1_out, selector4b_1_out_10, selector4b_1_out_11,
       selector4b_1_out_12, selector4b_1_out_13;

  mem4b mem4b_1 (
    .in_1(mem4b_2_out_7), .in_2(mem4b_2_out_8), .in_3(mem4b_2_out_9), .in_4(mem4b_2_out_10),
    .Read___Write(Clock), .out_7(out_8), .out_8(out_9), .out_9(out_10), .out_10(out_11), .Reset(Reset));
  add4b add4b_1 (
    .in_1(out_8), .in_2(out_9), .in_3(out_10), .in_4(out_11), .in_5(1'b1), .in_6(1'b0), .in_7(1'b0),
    .in_8(1'b0), .out_9(add4b_1_out_9), .out_10(add4b_1_out_10), .out_11(add4b_1_out_11),
    .out_12(add4b_1_out_12), .out_13(out_12));
  not not_1 (not_1_out, Clock);
  selector4b selector4b_1 (
    .in_1(add4b_1_out_9), .in_2(add4b_1_out_10), .in_3(add4b_1_out_11), .in_4(add4b_1_out_12), .in_5(in_2),
    .in_6(in_3), .in_7(Next_value), .in_8(in_5), .in_9(in_6), .out_10(selector4b_1_out_10),
    .out_11(selector4b_1_out_11), .out_12(selector4b_1_out_12), .out_13(selector4b_1_out_13));
  mem4b mem4b_2 (
    .in_1(selector4b_1_out_10), .in_2(selector4b_1_out_11), .in_3(selector4b_1_out_12),
    .in_4(selector4b_1_out_13), .Read___Write(not_1_out), .out_7(mem4b_2_out_7), .out_8(mem4b_2_out_8),
    .out_9(mem4b_2_out_9), .out_10(mem4b_2_out_10), .Reset(Reset));

  // Notes on the sheet:
  //   Use indicated next value
endmodule

module selector2b (
  input  in_1,
  input  in_2,
  input  in_3,
  input  in_4,
  input  in_5,
  output out_6,
  output out_7
);

  selector_1b selector_1b_1 (.in_1(in_1), .in_2(in_3), .in_3(in_5), .out_4(out_6));
  selector_1b selector_1b_2 (.in_1(in_2), .in_2(in_4), .in_3(in_5), .out_4(out_7));
endmodule

module registerManager4b (
  input  opcode,
  input  in_2,
  input  addr1,
  input  in_4,
  input  addr2,
  input  in_6,
  input  addr3,
  input  in_8,
  input  in_9,
  input  value,
  input  in_11,
  input  in_12,
  input  init,
  input  clock,
  input  reset,
  output out_16,
  output out_17,
  output out_18,
  output out_19,
  output out_20
);

  wire alu4b2op_1_out_10, alu4b2op_1_out_11, alu4b2op_1_out_12, alu4b2op_1_out_13, and_1_out, and_2_out,
       and_3_out, and_4_out, and_5_out, between4b_1_out_13, between4b_2_out_13, between4b_3_out_13,
       counter4b_1_out_3, counter4b_1_out_4, counter4b_1_out_5, counter4b_1_out_6, counter4b_1_out_7,
       mem1b_1_out_4, mem4b_1_out_7, mem4b_1_out_8, mem4b_1_out_9, mem4b_1_out_10, mem4b_2_out_7,
       mem4b_2_out_8, mem4b_2_out_9, mem4b_2_out_10, mem4b_3_out_7, mem4b_3_out_8, mem4b_3_out_9,
       mem4b_3_out_10, not_1_out, not_2_out, not_3_out, not_4_out, not_6_out, or_1_out, or_2_out, or_3_out,
       selector2b_1_out_6, selector2b_1_out_7, selector2b_2_out_6, selector2b_2_out_7, selector2b_3_out_6,
       selector2b_3_out_7, selector4b_1_out_10, selector4b_1_out_11, selector4b_1_out_12, selector4b_1_out_13;

  selector2b selector2b_1 (
    .in_1(addr1), .in_2(in_4), .in_3(addr2), .in_4(in_6), .in_5(between4b_1_out_13),
    .out_6(selector2b_1_out_6), .out_7(selector2b_1_out_7));
  or or_1 (or_1_out, reset, init);
  and and_1 (and_1_out, mem1b_1_out_4, clock, not_1_out);
  not not_1 (not_1_out, counter4b_1_out_7);
  selector2b selector2b_2 (
    .in_1(selector2b_1_out_6), .in_2(selector2b_1_out_7), .in_3(addr3), .in_4(in_8),
    .in_5(between4b_2_out_13), .out_6(selector2b_2_out_6), .out_7(selector2b_2_out_7));
  mem1b mem1b_1 (.Value_to_write(init), .Read___Write(not_2_out), .Reset(or_2_out), .out_4(mem1b_1_out_4));
  not not_2 (not_2_out, mem1b_1_out_4);
  or or_2 (or_2_out, counter4b_1_out_7, reset);
  counter4b counter4b_1 (
    .in_1(and_1_out), .in_2(or_1_out), .out_3(counter4b_1_out_3), .out_4(counter4b_1_out_4),
    .out_5(counter4b_1_out_5), .out_6(counter4b_1_out_6), .out_7(counter4b_1_out_7));
  not not_3 (not_3_out, in_2);
  selector2b selector2b_3 (
    .in_1(addr1), .in_2(in_4), .in_3(selector2b_2_out_6), .in_4(selector2b_2_out_7), .in_5(in_2),
    .out_6(selector2b_3_out_6), .out_7(selector2b_3_out_7));
  between4b between4b_1 (
    .in_1(1'b1), .in_2(1'b0), .in_3(1'b0), .in_4(1'b0), .in_5(counter4b_1_out_3), .in_6(counter4b_1_out_4),
    .in_7(counter4b_1_out_5), .in_8(counter4b_1_out_6), .in_9(1'b1), .in_10(1'b0), .in_11(1'b1),
    .in_12(1'b0), .out_13(between4b_1_out_13));
  selector4b selector4b_1 (
    .in_1(mem4b_3_out_7), .in_2(mem4b_3_out_8), .in_3(mem4b_3_out_9), .in_4(mem4b_3_out_10), .in_5(in_9),
    .in_6(value), .in_7(in_11), .in_8(in_12), .in_9(not_3_out), .out_10(selector4b_1_out_10),
    .out_11(selector4b_1_out_11), .out_12(selector4b_1_out_12), .out_13(selector4b_1_out_13));
  and and_2 (and_2_out, opcode, not_3_out);
  and and_3 (and_3_out, in_2, between4b_3_out_13);
  or or_3 (or_3_out, and_2_out, and_3_out);
  and and_4 (and_4_out, or_3_out, mem1b_1_out_4);
  between4b between4b_2 (
    .in_1(1'b0), .in_2(1'b1), .in_3(1'b0), .in_4(1'b0), .in_5(counter4b_1_out_3), .in_6(counter4b_1_out_4),
    .in_7(counter4b_1_out_5), .in_8(counter4b_1_out_6), .in_9(1'b0), .in_10(1'b0), .in_11(1'b1),
    .in_12(1'b0), .out_13(between4b_2_out_13));
  adrr4reg4b adrr4reg4b_1 (
    .in_1(selector4b_1_out_10), .in_2(selector4b_1_out_11), .Value_to_write(selector4b_1_out_12),
    .in_4(selector4b_1_out_13), .Read___Write(and_4_out), .in_6(selector2b_3_out_6),
    .Register_adress(selector2b_3_out_7), .out_9(out_16), .out_10(out_17), .out_11(out_18), .out_12(out_19),
    .Reset(reset));
  not not_4 (not_4_out, between4b_2_out_13);
  not not_5 (out_20, mem1b_1_out_4);
  not not_6 (not_6_out, between4b_1_out_13);
  and and_5 (and_5_out, between4b_1_out_13, not_4_out);
  between4b between4b_3 (
    .in_1(1'b1), .in_2(1'b1), .in_3(1'b0), .in_4(1'b0), .in_5(counter4b_1_out_3), .in_6(counter4b_1_out_4),
    .in_7(counter4b_1_out_5), .in_8(counter4b_1_out_6), .in_9(1'b1), .in_10(1'b1), .in_11(1'b0),
    .in_12(1'b0), .out_13(between4b_3_out_13));
  mem4b mem4b_1 (
    .in_1(out_16), .in_2(out_17), .in_3(out_18), .in_4(out_19), .Read___Write(not_6_out),
    .out_7(mem4b_1_out_7), .out_8(mem4b_1_out_8), .out_9(mem4b_1_out_9), .out_10(mem4b_1_out_10),
    .Reset(reset));
  mem4b mem4b_2 (
    .in_1(out_16), .in_2(out_17), .in_3(out_18), .in_4(out_19), .Read___Write(and_5_out),
    .out_7(mem4b_2_out_7), .out_8(mem4b_2_out_8), .out_9(mem4b_2_out_9), .out_10(mem4b_2_out_10),
    .Reset(reset));
  ALU4b2op alu4b2op_1 (
    .in_1(mem4b_1_out_7), .in_2(mem4b_1_out_8), .Number_1(mem4b_1_out_9), .in_4(mem4b_1_out_10),
    .in_5(mem4b_2_out_7), .in_6(mem4b_2_out_8), .Number_2(mem4b_2_out_9), .in_8(mem4b_2_out_10),
    .Add___Substract(opcode), .out_10(alu4b2op_1_out_10), .out_11(alu4b2op_1_out_11),
    .out_12(alu4b2op_1_out_12), .out_13(alu4b2op_1_out_13));
  mem4b mem4b_3 (
    .in_1(alu4b2op_1_out_10), .in_2(alu4b2op_1_out_11), .in_3(alu4b2op_1_out_12), .in_4(alu4b2op_1_out_13),
    .Read___Write(not_4_out), .out_7(mem4b_3_out_7), .out_8(mem4b_3_out_8), .out_9(mem4b_3_out_9),
    .out_10(mem4b_3_out_10), .Reset(reset));
endmodule

module counter4b (
  input  in_1,
  input  in_2,
  output out_3,
  output out_4,
  output out_5,
  output out_6,
  output out_7
);

  wire add4b_1_out_9, add4b_1_out_10, add4b_1_out_11, add4b_1_out_12, mem4b_2_out_7, mem4b_2_out_8,
       mem4b_2_out_9, mem4b_2_out_10, not_1_out;

  mem4b mem4b_1 (
    .in_1(mem4b_2_out_7), .in_2(mem4b_2_out_8), .in_3(mem4b_2_out_9), .in_4(mem4b_2_out_10),
    .Read___Write(in_1), .out_7(out_3), .out_8(out_4), .out_9(out_5), .out_10(out_6), .Reset(in_2));
  add4b add4b_1 (
    .in_1(out_3), .in_2(out_4), .in_3(out_5), .in_4(out_6), .in_5(1'b1), .in_6(1'b0), .in_7(1'b0),
    .in_8(1'b0), .out_9(add4b_1_out_9), .out_10(add4b_1_out_10), .out_11(add4b_1_out_11),
    .out_12(add4b_1_out_12), .out_13(out_7));
  not not_1 (not_1_out, in_1);
  mem4b mem4b_2 (
    .in_1(add4b_1_out_9), .in_2(add4b_1_out_10), .in_3(add4b_1_out_11), .in_4(add4b_1_out_12),
    .Read___Write(not_1_out), .out_7(mem4b_2_out_7), .out_8(mem4b_2_out_8), .out_9(mem4b_2_out_9),
    .out_10(mem4b_2_out_10), .Reset(in_2));
endmodule

module inf4b (
  input  in_1,
  input  in_2,
  input  in_3,
  input  in_4,
  input  in_5,
  input  in_6,
  input  in_7,
  input  in_8,
  output out_9
);

  wire and_1_out, not_1_out, or_1_out, selector_1b_1_out_4, selector_1b_2_out_4, xor_1_out, xor_2_out,
       xor_3_out;

  and and_1 (and_1_out, in_1, in_5);
  not not_1 (not_1_out, in_1);
  or or_1 (or_1_out, not_1_out, and_1_out);
  xor xor_1 (xor_1_out, in_2, in_6);
  selector_1b selector_1b_1 (.in_1(or_1_out), .in_2(in_6), .in_3(xor_1_out), .out_4(selector_1b_1_out_4));
  xor xor_2 (xor_2_out, in_3, in_7);
  selector_1b selector_1b_2 (.in_1(selector_1b_1_out_4), .in_2(in_7), .in_3(xor_2_out), .out_4(selector_1b_2_out_4));
  selector_1b selector_1b_3 (.in_1(selector_1b_2_out_4), .in_2(in_8), .in_3(xor_3_out), .out_4(out_9));
  xor xor_3 (xor_3_out, in_4, in_8);
endmodule

module between4b (
  input  in_1,
  input  in_2,
  input  in_3,
  input  in_4,
  input  in_5,
  input  in_6,
  input  in_7,
  input  in_8,
  input  in_9,
  input  in_10,
  input  in_11,
  input  in_12,
  output out_13
);

  wire inf4b_1_out_9, inf4b_2_out_9;

  inf4b inf4b_1 (
    .in_1(in_1), .in_2(in_2), .in_3(in_3), .in_4(in_4), .in_5(in_5), .in_6(in_6), .in_7(in_7), .in_8(in_7),
    .out_9(inf4b_1_out_9));
  inf4b inf4b_2 (
    .in_1(in_5), .in_2(in_6), .in_3(in_7), .in_4(in_8), .in_5(in_9), .in_6(in_10), .in_7(in_11),
    .in_8(in_12), .out_9(inf4b_2_out_9));
  and and_1 (out_13, inf4b_1_out_9, inf4b_2_out_9);
endmodule

module equal4b (
  input  in_1,
  input  in_2,
  input  in_3,
  input  in_4,
  input  in_5,
  input  in_6,
  input  in_7,
  input  in_8,
  output out_9
);

  between4b between4b_1 (
    .in_1(in_5), .in_2(in_6), .in_3(in_7), .in_4(in_8), .in_5(in_1), .in_6(in_2), .in_7(in_3), .in_8(in_4),
    .in_9(in_5), .in_10(in_6), .in_11(in_7), .in_12(in_8), .out_13(out_9));
endmodule
